# Fritzing sketch pico-w-grow-kit-adapter (saved by Fritzing 0.9.6b)

parts:
  JP1 = Header 10 [package=1x10-2mm-smd]
  JP2 = Header 10 [package=1x10-2mm-smd]
  JP3 = Header 10 [package=1x10-2mm-smd]
  JP4 = Header 10 [package=1x10-2mm-smd]
  JP5 = Header 10 [package=1x10-2mm-smd]
  JP6 = Header 10 [package=1x10-2mm-smd]
  JP7 = Header 10 [package=1x10-2mm-smd]
  JP8 = Header 10 [package=1x10-2mm-smd]
  Part1 = Adafruit Perma-Proto HAT [part_number="Adafruit #2314 and #2310"]

nets:
  N1: JP1.1, Part1.N$2#161
  N2: JP1.2, Part1.N$3#166
  N3: JP1.3, Part1.N$4
  N4: JP1.4, Part1.N$5#176
  N5: JP1.5, Part1.N$6#181
  N6: JP1.6, Part1.N$8
  N7: JP1.7, Part1.N$7
  N8: JP1.8, Part1.N$9
  N9: JP1.9, Part1.N$10
  N10: JP1.10, Part1.N$11
  N11: JP2.1, Part1.N$12
  N12: JP2.2, Part1.N$13
  N13: JP2.3, Part1.N$14
  N14: JP2.4, Part1.N$15
  N15: JP2.6, Part1.N$18#236
  N16: JP2.7, Part1.N$17
  N17: JP2.8, Part1.N$19#241
  N18: JP2.9, Part1.N$20
  N19: JP2.10, Part1.N$22#256
  N20: JP3.1, Part1.N$61
  N21: JP3.2, Part1.N$59
  N22: JP3.3, Part1.N$60
  N23: JP3.4, Part1.N$58
  N24: JP3.5, Part1.N$57
  N25: JP3.6, Part1.N$56
  N26: JP3.7, Part1.N$55
  N27: JP3.8, Part1.N$53
  N28: JP3.9, Part1.N$54
  N29: JP3.10, Part1.N$52#330
  N30: JP4.1, Part1.N$51
  N31: JP4.2, Part1.N$49
  N32: JP4.3, Part1.N$50
  N33: JP4.4, Part1.N$48#310
  N34: JP4.5, Part1.N$47#305
  N35: JP4.6, Part1.N$46
  N36: JP4.7, Part1.N$45
  N37: JP4.8, Part1.N$44
  N38: JP4.9, Part1.N$43
  N39: JP4.10, Part1.N$42
  N40: JP5.1, JP5.2, Part1.5.0V, Part1.N$22#257
  N41: JP5.3, JP5.7, JP5.10, JP6.5, JP6.7, JP7.5, JP8.3, JP8.10, Part1.GND, Part1.N$19#243
  N42: JP5.4, Part1.TXD
  N43: JP5.5, Part1.RXD
  N44: JP5.6, Part1.GPIO18
  N45: JP5.8, Part1.GPIO23
  N46: JP5.9, Part1.GPIO24
  N47: JP6.1, Part1.GPIO25
  N48: JP6.2, Part1.SPI_CE0, Part1.N$52#329
  N49: JP6.3, Part1.SPI_CE1, Part1.N$3#170
  N50: JP6.4, Part1.EECLK
  N51: JP6.6, Part1.GPIO12
  N52: JP6.8, Part1.GPIO16
  N53: JP6.9, Part1.GPIO20
  N54: JP6.10, Part1.GPIO21
  N55: JP7.1, JP7.9, Part1.3.3V, Part1.N$18#239
  N56: JP7.2, Part1.SDA, Part1.N$47#302
  N57: JP7.3, Part1.SCL, Part1.N$48#306
  N58: JP7.4, Part1.GPIO4
  N59: JP7.6, Part1.GPIO17
  N60: JP7.7, Part1.GPIO27
  N61: JP7.8, Part1.GPIO22
  N62: JP7.10, Part1.SPI_MOSI, Part1.N$6#184
  N63: JP8.1, Part1.SPI_MISO, Part1.N$2#165
  N64: JP8.2, Part1.SPI_SCLK, Part1.N$5#180
  N65: JP8.4, Part1.EEDATA
  N66: JP8.5, Part1.GPIO5
  N67: JP8.6, Part1.GPIO6
  N68: JP8.7, Part1.GPIO13
  N69: JP8.8, Part1.GPIO19
  N70: JP8.9, Part1.GPIO26

custom parts:
  Adafruit Perma-Proto HAT: To kick off the Adafruit HAT party, we have this Perma-Proto inspired plug in daughter board. It has a grid of 0.1" prototyping soldering holes for attaching chips, resistors, LED, potentiometers and more. The holes are connected underneath with traces to mimic the solderless breadboards you're familiar. There's also long power strips for +3V, +5V and Ground connections to the Pi. Near the top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
